# Fritzing sketch LED깜박이기(Senser) (saved by Fritzing 0.9.3b)
breadboards: 1

parts:
  부품1 = Arduino Uno (Rev3)
  R1 = Resistor [tolerance=±5% resistance=220 package=THT]
  R2 = Photocell (LDR) [package=THT]

nets:
  N1: 부품1.A0, R1.Pin_0, R2.pin_0
  N2: 부품1.5V, R1.Pin_1
  N3: 부품1.GND, R2.pin_1
